# Fritzing sketch Gandalfs_Magic_Staff (saved by Fritzing 0.9.3b)

parts:
  R1 = Resistor [tolerance=±5% resistance=220 package=THT]
  Q1 = NPN-Transistor [part_number=Transistor package="TO92 [THT]"]
  J1 = Piezo Speaker [part_number=Speaker]
  Part3 = 12 NeoPixel Ring [part_number=1643]
  Part4 = Adafruit Pro Trinket 3.3V 12MHz [part_number="Adafruit #2010"]
  Part5 = Lithium Ion Polymer Battery 3.7v 500mAh [part_number=1578]
  LED1 = LED - 5mm [color="Red (633nm)" part_number=Array package="5 mm [THT]"]
  D1 = Diode [part_number="Flyback Diode" package=diode-1n4148]
  Q2 = NPN-Transistor [part_number=Transistor package="TO92 [THT]"]
  R2 = Resistor [tolerance=±5% resistance=220 package=THT]
  Part2 = Adafruit Pro Trinket LiIon/LiPoly Backpack [part_number="Li-Poly Charger"]
  S2 = Reed switch [package=THT]
  S3 = Reed switch [part_number=part_2 package=THT]
  S4 = Reed switch [package=THT]
  S5 = Reed switch [package=THT]
  Q3 = NPN-Transistor [part_number=Transistor package="TO92 [THT]"]
  D2 = Diode [part_number="Flyback Diode" package=diode-1n4148]
  S1 = Reed switch [package=THT]
  IC3 = DIP - 8 pins [part_number="HK 23f 5v relay" chip_label=Relay package="DIP (Dual Inline) [THT]"]
  IC4 = DIP - 8 pins [part_number="HK 23f 5v relay" chip_label=Relay package="DIP (Dual Inline) [THT]"]
  Part7 = Adafruit Music Maker FeatherWing with Amp [part_number="Adafruit #3436"]
  U2 = PIC-ICSP-Mini [package=pic-icsp-mini]
  Generic_BlueTooth_Transmitter2 = Generic Bluetooth Transmitter [chip_label="Bluetooth Transmitter" package=THT]
  J2 = Piezo Speaker [part_number=Speaker]  # not connected
  Part6 = Mono 2.5W Class D Audio Amplifier - PAM8302
  S6 = Reed switch [package=THT]

nets:
  N1: R1.Pin_0, Q1.B
  N2: R1.Pin_1, Part4.D9, U2.Signal_LED
  N3: Q1.E, Q2.E, U2.GND
  N4: Q1.C, D1.A, IC4.Coil_2
  N5: J1.pin1, Part6.VO-
  N6: J1.pin2, S6.pin_2
  N7: Part3.IN, Part4.D10
  VDD: Part3.VDD, Part4.VBAT, Part2.VBAT, Generic_BlueTooth_Transmitter2.VCC
  GND: Part3.GND, Part4.GND, Part5.negative, LED1.cathode, Part2.GND, S2.pin_2, S3.pin_2, S4.pin_2, S5.pin_2, Part7.GND, Generic_BlueTooth_Transmitter2.GND, Part6.GND
  N8: Part4.VBUS, Part2.VBUS
  +3V3: Part4.+3V3, Part7.3.3V, Part6.VCC
  N9: Part4.D8, Part7.MP3CS
  N10: Part4.D6, Part7.XDCS
  N11: Part4.D4, Part7.SD_CS
  N12: Part4.D3, Part7.DREQ
  N13: Part4.D11, Part7.MOSI
  N14: Part4.D12, Part7.MISO
  N15: Part4.D13, Part7.SCLK
  N16: Part4.A0, Q3.B
  N17: Part4.A1, S5.pin_1
  N18: Part4.A2, S4.pin_1
  N19: Part4.A3, S3.pin_1
  N20: Part4.A4, S2.pin_1
  N21: Part5.positive, D1.C, Part2.SW1, D2.C, S1.pin_1, IC3.Coil_1, IC3.Common, IC4.Coil_1, IC4.Common, U2.VCC
  N22: LED1.anode, IC4.Normall_Open, U2.VCC_LED
  N23: Q2.B, R2.Pin_0
  N24: Q2.C, D2.A, IC3.Coil_2
  N25: R2.Pin_1, S1.pin_2
  N26: Part2.SW2, IC3.Normall_Open, U2.VCC_Trinket
  N27: Q3.E, Generic_BlueTooth_Transmitter2.sw_Power#1
  N28: Q3.C, Generic_BlueTooth_Transmitter2.sw_Power#0
  N29: Part7.OUT_LEFT-, Generic_BlueTooth_Transmitter2.Spkr_GND, Part6.AIN-
  N30: Part7.OUT_LEFT+, Generic_BlueTooth_Transmitter2.Spkr_Right, Part6.AIN+
  N31: Part7.OUT_RIGHT+, Generic_BlueTooth_Transmitter2.Spkr_Left
  N32: Part6.VO+, S6.pin_1

notes:
  Reed Switches coloured to match ribbon cable.
  Reed Switches:
  The secret is in the switches
  Increment
  Decrement
  Toggle
  Functions
  Reed Switch: Power On/Off Staff
  Reed switch triggers the Transistor Transistor energizes the relay.
  Relay passes power to Arduino
  Audio Amplifier
  Switch for LED Array
  Arduino triggers the Transistor which in turn energizes the relay
  which passes power from the battery to the LED Array.
  Main Power Switch
  Magnet closes circuit
  Optional second speaker
  Needs amplifier.
  Speaker Switch

custom parts:
  12 NeoPixel Ring: 12 ultra bright smart LED NeoPixels are arranged in a circle with 1.5" (37mm) outer diameter. The rings are 'chainable' - connect the output pin of one to the input pin of another. Use only one microcontroller pin to control as many as you can chain together! Each LED is addressable as the driver chip is inside the LED. Each one has ~18mA constant current drive so the color will be very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
  Adafruit Pro Trinket 3.3V 12MHz: rinket's got a big sister in town - the Pro Trinket 3V! Pro Trinket combines everything you love about Trinket with the familiarity of the core Arduino chip, the ATmega328. It's like an Arduino Pro Mini with more pins and USB tossed in. Trinket's a year old now, and while its been great to see tons of tiny projects, sometimes you just need more pins, more FLASH, and more RAM. That's why we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
  Lithium Ion Polymer Battery 3.7v 500mAh: Lithium ion polymer (also known as 'lipo' or 'lipoly') batteries are thin, light and powerful. The output ranges from 4.2V when completely charged to 3.7V. This battery has a capacity of 500mAh for a total of about 1.9 Wh. The batteries come pre-attached with a genuine 2-pin JST-PH connector as shown and include the necessary protection circuitry.
  Adafruit Pro Trinket LiIon/LiPoly Backpack: If you have a Pro Trinket you probably know it's the perfect little size for a portable project. This LiPoly backpack makes it really easy to do! Instead of wiring 2 or 3 boards together to make a charging system, this little PCB sits on top of the Pro Trinket and allows a LiPoly/LiIon battery to plug in. When the Pro Trinket USB port is powered, the battery is recharged automatically. Unplug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
  DIP - 8 pins: A DIP stand-in part for whatever IC you want. With 8 pins on a 300mil dual inline package (DIP) footprint.
  Adafruit Music Maker FeatherWing with Amp: Bend all audio files to your will with the Adafruit Music Maker FeatherWing + Amplifier! It's a fun-size version of our Music Maker shield for Arduino, and similar to our other Music Maker FeatherWing, but this one is even better - with an on-board 3 Watt amplifier! This powerful wing features the VS1053, an encoding/decoding (codec) chip that can decode a wide variety of audio formats such as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
  PIC-ICSP-Mini: PIC-ICSP-Mini Miniature 5-pin connection for temporary programming of PICs. Use this device in your design to save space. Program the PIC with this adapter Spark Fun Electronics SKU : BOB-00194
  Generic Bluetooth Transmitter: Simply Bluetooth Transmitter
  Mono 2.5W Class D Audio Amplifier - PAM8302: A super small but powerful mono amplifier able to deliver up to 2.5 Watts into 4-8 ohm impedance speakers. Inside the miniature chip is a class D controller, able to run from 2.0V-5.5VDC. Since the amp is a class D, its very efficient (over 90% efficient when driving an 8Ω speaker at over half a Watt) - making it perfect for portable and battery-powered projects.
